# Fritzing sketch Dazzler-noaudio (saved by Fritzing 0.9.3b)
stripboards: 1

parts:
  IC2 = IC, DIP package, 28 pins [chip_label=PIC32MX128B]
  IC3 = IC, DIP package, 14 pins [chip_label=74HC08]
  R2 = Resistor [tolerance=±5% resistance=470 package=THT]
  R3 = Resistor [tolerance=±5% resistance=470 package=THT]
  R4 = Resistor [tolerance=±5% resistance=470 package=THT]
  R5 = Resistor [tolerance=±5% resistance=220 package=THT]
  R6 = Resistor [tolerance=±5% resistance=220 package=THT]
  R7 = Resistor [tolerance=±5% resistance=220 package=THT]
  D7 = Rectifier Diode [part_number=1N4148 package="300 mil [THT]"]
  D8 = Rectifier Diode [part_number=1N4148 package="300 mil [THT]"]
  D9 = Rectifier Diode [part_number=1N4148 package="300 mil [THT]"]
  D10 = Rectifier Diode [part_number=1N4148 package="300 mil [THT]"]
  R8 = Resistor [tolerance=±5% resistance=680 package=THT]
  R9 = Resistor [tolerance=±5% resistance=75 package=THT]
  R10 = Resistor [tolerance=±5% resistance=330 package=THT]
  R11 = Resistor [tolerance=±5% resistance=150 package=THT]
  ICSP = female pin header, 6 pins [form="♀ (female)"]
  R12 = Resistor [tolerance=±5% resistance=4.7k package=THT]
  C8 = Ceramic Capacitor [capacitance=100nF voltage=10V package="100 mil [THT, multilayer]"]
  C10 = Ceramic Capacitor [capacitance=27pF voltage=10V package="100 mil [THT, multilayer]"]
  IC4 = IC, DIP package, 16 pins [chip_label=74HC4053]
  VGA = female pin header, 6 pins [form="♀ (female)"]
  C11 = Ceramic Capacitor [capacitance=100nF voltage=10V package="100 mil [THT, multilayer]"]
  USB = female pin header, 4 pins [form="♀ (female)"]
  U2 = Voltage Regulator - 3.3V [package="TO220 [THT]"]
  IC5 = IC, DIP package, 16 pins [chip_label=74HC165]
  JOY1 = female pin header, 8 pins [form="♀ (female)"]
  C13 = Electrolytic Capacitor [capacitance=10μF package="0605 [SMD, electrolytic]"]
  R13 = Resistor [tolerance=±5% resistance=10k package=THT]
  R14 = Resistor [tolerance=±5% resistance=10k package=THT]
  R15 = Resistor [tolerance=±5% resistance=10k package=THT]
  R16 = Resistor [tolerance=±5% resistance=10k package=THT]
  R17 = Resistor [tolerance=±5% resistance=10k package=THT]
  R18 = Resistor [tolerance=±5% resistance=10k package=THT]
  R19 = Resistor [tolerance=±5% resistance=10k package=THT]
  R20 = Resistor [tolerance=±5% resistance=10k package=THT]
  S3_(Reset) = Pushbutton [package="[THT]"]
  LED4 = LED - 3mm [color="Green (555nm)" package="3 mm [THT]"]
  R21 = Resistor [tolerance=±5% resistance=150 package=THT]
  S4_(Test) = Pushbutton [package="[THT]"]
  C9 = Ceramic Capacitor [capacitance=27pF voltage=10V package="100 mil [THT, multilayer]"]
  XTAL2 = Crystal [frequency="8 MHz" package=THT]
  C12 = Tantalum Capacitor [capacitance="1 μF" package="200 mil [THT, tantalum]"]
  JOY2 = female pin header, 8 pins [form="♀ (female)"]

nets:
  N1: IC2.pin1, ICSP.pin1, R12.Pin_1, S3_(Reset).Pin_3, S3_(Reset).Pin_4
  JOY2X: IC2.pin2, ICSP.pin4, JOY2.pin7
  JOY2Y: IC2.pin3, ICSP.pin5, JOY2.pin8
  RGBI-R: IC2.pin4, IC3.pin1, R5.Pin_1, D7.anode
  RGBI-G: IC2.pin5, IC3.pin10, R6.Pin_1, D8.anode
  RGBI-B: IC2.pin6, IC3.pin13, R7.Pin_1, D9.anode
  RGBI-I: IC2.pin7, IC3.pin2, IC3.pin9, IC3.pin12, D10.anode
  GND: IC2.pin8, IC2.pin19, IC2.pin27, IC3.pin4, IC3.pin5, IC3.pin7, ICSP.pin3, C8.0, C10.0, IC4.pin6, IC4.pin7, IC4.pin8, VGA.pin6, C11.1, USB.pin4, U2.GND, IC5.pin8, IC5.pin10, IC5.pin15, JOY1.pin2, C13.-, S3_(Reset).Pin_1, S3_(Reset).Pin_2, R21.Pin_0, S4_(Test).Pin_3, S4_(Test).Pin_4, C9.0, C12.-, JOY2.pin2
  N2: IC2.pin9, C10.1, XTAL2.pin_0
  N3: IC2.pin10, C9.1, XTAL2.pin_1
  BSHIFT: IC2.pin11, IC5.pin1
  COLOR: IC2.pin12, IC4.pin9, IC4.pin10, IC4.pin11
  3.3V: IC2.pin13, IC2.pin23, IC2.pin28, IC3.pin14, ICSP.pin2, R12.Pin_0, C8.1, IC4.pin16, C11.0, U2.output_voltage, IC5.pin16, JOY1.pin1, C13.+, R13.Pin_0, R14.Pin_0, R15.Pin_0, R16.Pin_0, R17.Pin_0, R18.Pin_0, R19.Pin_0, R20.Pin_0, LED4.anode, JOY2.pin1
  BDATA: IC2.pin14, IC5.pin9
  N4: IC2.pin15, USB.pin3, U2.input_voltage
  HSYNC: IC2.pin16, VGA.pin5
  TEST: IC2.pin17, S4_(Test).Pin_1, S4_(Test).Pin_2
  VSYNC: IC2.pin18, VGA.pin4
  N5: IC2.pin20, C12.+
  N6: IC2.pin21, USB.pin2
  N7: IC2.pin22, USB.pin1
  BCLK: IC2.pin24, IC5.pin2
  JOY1Y: IC2.pin25, JOY1.pin8
  JOY1X: IC2.pin26, JOY1.pin7
  N8: IC3.pin3, R2.Pin_1
  N9: IC3.pin8, R3.Pin_1
  N10: IC3.pin11, R4.Pin_1
  N11: R2.Pin_0, R5.Pin_0, IC4.pin1
  N12: R3.Pin_0, R6.Pin_0, IC4.pin13
  N13: R4.Pin_0, R7.Pin_0, IC4.pin3
  N14: D7.cathode, R8.Pin_1
  N15: D8.cathode, R10.Pin_1
  N16: D9.cathode, R11.Pin_1
  N17: D10.cathode, R9.Pin_1
  N18: R8.Pin_0, R9.Pin_0, R10.Pin_0, R11.Pin_0, IC4.pin2, IC4.pin5, IC4.pin12
  N19: IC4.pin4, VGA.pin3
  N20: IC4.pin14, VGA.pin2
  N21: IC4.pin15, VGA.pin1
  N22: IC5.pin3, R19.Pin_1, JOY2.pin6
  N23: IC5.pin4, R20.Pin_1, JOY2.pin5
  N24: IC5.pin5, R18.Pin_1, JOY2.pin4
  N25: IC5.pin6, R17.Pin_1, JOY2.pin3
  N26: IC5.pin11, JOY1.pin6, R13.Pin_1
  N27: IC5.pin12, JOY1.pin5, R14.Pin_1
  N28: IC5.pin13, JOY1.pin4, R15.Pin_1
  N29: IC5.pin14, JOY1.pin3, R16.Pin_1
  N30: LED4.cathode, R21.Pin_1

notes:
  GND
  3V3
  Y
  B2
  B4
  B1
  X
  B3
  D- (2)
  D+ (3)
  5V (1)
  D+
  GND (4)
  R (1)
  R
  G (2)
  B (3)
  VSYNC (14)
  HSYNC (13)
  GND (5-10)
  MCLR (1)
  VDD (2)
  GND (3)
  PGD (4)
  PGC (5)
