# Fritzing sketch Joystick (saved by Fritzing 0.9.3b)
stripboards: 1

parts:
  J1 = female pin header, 8 pins [form="♀ (female)"]
  S1 = Pushbutton [package="[THT]"]
  S2 = Pushbutton [package="[THT]"]
  S3 = Pushbutton [package="[THT]"]
  S4 = Pushbutton [package="[THT]"]
  C1 = Ceramic Capacitor [capacitance=100nF voltage=10V package="100 mil [THT, multilayer]"]
  U1 = Thumb Joystick [package=joystick]
  C2 = Ceramic Capacitor [capacitance=100nF voltage=10V package="100 mil [THT, multilayer]"]

nets:
  N1: J1.pin1, U1.V+, U1.H+
  N2: J1.pin2, S1.Pin_1, S1.Pin_2, S2.Pin_1, S2.Pin_2, S3.Pin_1, S3.Pin_2, S4.Pin_1, S4.Pin_2, C1.0, U1.H-, U1.V-, C2.0
  N3: J1.pin3, S4.Pin_3, S4.Pin_4
  N4: J1.pin4, S3.Pin_3, S3.Pin_4
  N5: J1.pin5, S2.Pin_3, S2.Pin_4
  N6: J1.pin6, S1.Pin_3, S1.Pin_4
  N7: J1.pin7, C1.1, U1.H
  N8: J1.pin8, U1.V, C2.1

notes:
  3V3
  GND
  B4
  B3
  B2
  B1
  X
  Y
